# Fritzing sketch dispenser-with-just-resistors (saved by Fritzing 1.0.2b)
circuit board: 8cm x 6cm
breadboards: 1

parts:
  USB-ESP = Header 5x2 [package=2x5-ra]
  R20 = Resistor [tolerance=±20% power=0.25 resistance=47 package=THT]
  R1servo = Resistor [tolerance=±20% power=0.25 resistance=47 package=THT]
  ESP32-30pin1 = LuaNode32 / ESP32 [part_number=ESP32S-PIN30]
  USB-S = Header 5x2 [package=2x5-ra]
  R2Servo = TRIMPOT [maximum_resistance=5kΩ knob_status=50% power=0.5W package=3362u-2]
  R2ESP = TRIMPOT [maximum_resistance=5kΩ knob_status=50% power=0.5W package=3362u-2]
  servo = Basic Servo

nets:
  GND: USB-ESP.1, R20.Pin_1, ESP32-30pin1.GND, USB-S.1, R2Servo.WIPER, servo.gnd
  N1: USB-ESP.9, ESP32-30pin1.Vin, R2ESP.CCW
  N2: R20.Pin_0, R2ESP.WIPER
  N3: R1servo.Pin_0, USB-S.9
  N4: R1servo.Pin_1, R2Servo.CCW
  N5: ESP32-30pin1.D19, servo.pulse
  N6: R2Servo.CW, servo.vcc

notes:
  resistor for servo. Servo doesn't take current at all in idle mode, so we need to take full 70mA through resistor
  Adding resistor to be able to adjust current taken.
  If resistor is set to 200R, then current is 25mA
  If resistor is set to 0, then additional current is 100mA
  resistor for esp32 circuit. I assume that esp32 takes 35mAh, so need to draw additional 35mAh
  also adding 200R resistor to be able to adjust current taken.
  w502 3297

custom parts:
  LuaNode32 / ESP32: New Image for LuaNode32 DOIT ESP32 DEVKIT V1. Base parts from LuaNode32 / ESP32 ESP32 based LuaNode32 by G.Noorlander DOIT Esp32 DevKit v1 (30 pins long, 11 pins width) by Werner Rothschopf (modified by vanepp Dec 2018)
