# Fritzing sketch dispenser-with-keepalive (saved by Fritzing 0.9.10b)
circuit board: 5.8cm x 4.5cm
perfboards: 1

parts:
  ESP32-30pin1 = esp32
  C6 = Capacitor [part_number=0.1UF package=cap-pth-small-kit]
  C9 = Capacitor [part_number=0.1UF package=cap-pth-small-kit]
  R17 = Resistor [tolerance=±5% resistance=220k power=0.25 package=THT]
  R16 = Resistor [tolerance=±20% resistance=22k power=0.25 package=THT]
  R13 = Resistor [tolerance=±20% resistance=47 power=0.25 package=THT]
  R15 = Resistor [tolerance=±5% resistance=100 power=0.25 package=THT]
  LED2 = LED - 3mm [color="Yellow (585nm)" current=0.030 package="3 mm [THT]"]
  LED3 = LED - 3mm [color="Red (633nm)" current=0.030 package="3 mm [THT]"]
  R21 = Resistor [tolerance=±5% resistance=5100 power=0.25 package=THT]
  R18 = Resistor [tolerance=±5% resistance=47 power=0.25 package=THT]
  C4 = Tantalum Capacitor [capacitance=20µF voltage=35V package="100 mil [THT, tantalum]"]
  USB-S = Header 5x2 [package=2x5-ra]
  J1 = Basic Servo
  R20 = Resistor [tolerance=±5% resistance=22k power=0.25 package=THT]
  R22 = Resistor [tolerance=±5% resistance=220k power=0.25 package=THT]
  R19 = Resistor [tolerance=±5% resistance=100 power=0.25 package=THT]
  USB-ESP = Header 5x2 [package=2x5-ra]
  Q2 = PNP-Transistor [package="TO92 [THT]"]
  R14 = Resistor [tolerance=±5% power=0.25 resistance=5100 package=THT]
  U7 = General purpose bipolar Timer [package=dil-08]
  U3 = General purpose bipolar Timer [package=dil-08]
  Q3 = PNP-Transistor [package="TO92 [THT]"]
  C7 = Tantalum Capacitor [capacitance=20µF voltage=35V package="100 mil [THT, tantalum]"]

nets:
  N1: ESP32-30pin1.d19, J1.pulse
  GND: ESP32-30pin1.gnd, ESP32-30pin1.GND, C6.2, C9.2, R13.Pin_1, LED2.cathode, LED3.cathode, R18.Pin_1, C4.-, USB-S.1, J1.gnd, USB-ESP.1, U7.GND, U3.GND, C7.-
  N2: ESP32-30pin1.Vin, R17.Pin_0, USB-ESP.9, Q2.E, U3._RES, U3.VCC+
  N3: C6.1, U3.CON
  N4: C9.1, U7.CON
  N5: R17.Pin_1, R16.Pin_0, U3.DIS
  N6: R16.Pin_1, C4.+, U3.TRI, U3.TRE
  N7: R13.Pin_0, R15.Pin_0, Q2.C
  N8: R15.Pin_1, LED2.anode
  N9: LED3.anode, R19.Pin_1
  N10: R21.Pin_0, U7.OUT
  N11: R21.Pin_1, Q3.B
  N12: R18.Pin_0, R19.Pin_0, Q3.C
  N13: USB-S.9, J1.vcc, R22.Pin_0, U7._RES, U7.VCC+, Q3.E
  N14: R20.Pin_0, R22.Pin_1, U7.DIS
  N15: R20.Pin_1, C7.+
  N16: Q2.B, R14.Pin_1
  N17: R14.Pin_0, U3.OUT
  N18: U7.TRI, U7.TRE

notes:
  keepalive for servo circuit
  keepalive for esp32 circuit

custom parts:
  esp32: based on work of Roman Minyaylov, at https://github.com/roman-minyaylov/nodemcu-v3-fritzing
