# Fritzing sketch usb-keepalive-pnp-for-esp32 (saved by Fritzing 0.9.6b)
breadboards: 1

parts:
  R1 = Resistor [tolerance=±5% resistance=220k package="0603 [SMD]"]
  C2 = Electrolytic Capacitor [capacitance=10µF voltage=35V package="200 mil [THT, electrolytic]"]
  U1 = General purpose bipolar Timer [package=dil-08]
  X1 = Mini-USB _B_ connector with 5th pin broken out. [package=usb-minib]
  C1 = Capacitor [part_number=0.1UF package=cap-pth-small-kit]
  U2 = Mini-USB _B_ connector with 5th pin broken out. [package=usb-micro_b]
  R9 = Resistor [tolerance=±5% resistance=47 package="2512 [SMD]"]
  R10 = Resistor [tolerance=±5% resistance=100 package="2512 [SMD]"]
  LED1 = smd LED [color="Yellow (592nm)" package="0805 [SMD]"]
  Q1 = PNP-Transistor [part_number=s8550 package="TO92 [THT]"]
  R11 = Resistor [tolerance=±5% resistance=5100 package="2512 [SMD]"]
  R12 = Resistor [tolerance=±5% resistance=22k package="2512 [SMD]"]
  C3 = Electrolytic Capacitor [capacitance=10µF voltage=35V package="200 mil [THT, electrolytic]"]

nets:
  N1: R1.Pin_0, U1._RES, U1.VCC+, X1.VBUS, U2.VCC, Q1.E
  N2: R1.Pin_1, U1.DIS, R12.Pin_0
  GND: C2.-, U1.GND, C1.2, U2.GND, R9.Pin_1, LED1.cathode, C3.-
  N3: C2.+, U1.TRI, U1.TRE, R12.Pin_1, C3.+
  N4: U1.OUT, R11.Pin_0
  N5: U1.CON, C1.1
  N6: R9.Pin_0, R10.Pin_0, Q1.C
  N7: R10.Pin_1, LED1.anode
  N8: Q1.B, R11.Pin_1

notes:
  works with both esp32 and without esp32
  esp32 sometimes starts with "brownout detected" but then situation becames stable

custom parts:
  Mini-USB _B_ connector with 5th pin broken out.: Socket micro-USB B 5P, 629105150521, Würth Elektronik
