# Fritzing sketch usb-keepalive (saved by Fritzing 0.9.6b)
breadboards: 1

parts:
  R1 = Resistor [tolerance=±5% resistance=220k package="0603 [SMD]"]
  C2 = Electrolytic Capacitor [capacitance=47µF voltage=35V package="200 mil [THT, electrolytic]"]
  U1 = General purpose bipolar Timer [package=dil-08]
  X1 = Mini-USB _B_ connector with 5th pin broken out. [package=usb-minib]
  C1 = Capacitor [part_number=0.1UF package=cap-pth-small-kit]
  U2 = Mini-USB _B_ connector with 5th pin broken out. [package=usb-micro_b]
  R8 = TRIMPOT [part_number=10K package=3386u]
  R9 = Resistor [tolerance=±5% resistance=22 package="2512 [SMD]"]
  R10 = Resistor [tolerance=±5% resistance=220 package="2512 [SMD]"]
  LED1 = smd LED [color="Yellow (592nm)" package="0805 [SMD]"]

nets:
  N1: R1.Pin_0, U1._RES, U1.VCC+, X1.VBUS, U2.VCC, R9.Pin_1, LED1.anode
  N2: R1.Pin_1, U1.DIS, R8.WIPER
  GND: C2.-, U1.GND, C1.2, U2.GND
  N3: C2.+, U1.TRI, U1.TRE, R8.CW
  N4: U1.OUT, R9.Pin_0, R10.Pin_0
  N5: U1.CON, C1.1
  N6: R10.Pin_1, LED1.cathode

custom parts:
  Mini-USB _B_ connector with 5th pin broken out.: Socket micro-USB B 5P, 629105150521, Würth Elektronik
