# Fritzing sketch button (saved by Fritzing 0.9.6b)
breadboards: 2

parts:
  ESP32-30pin1 = esp32
  S1 = Round Pushbutton
  R1 = Resistor [tolerance=±5% resistance=6.8k package="0603 [SMD]"]
  LED1 = LED - 5mm [color="Red (633nm)" current=0.030 package="5 mm [THT]"]
  R2 = Resistor [tolerance=±5% resistance=220 package="0603 [SMD]"]
  R3 = Resistor [tolerance=±5% resistance=150 power=0.25 package=THT]

nets (from the schematic view):
  N1: ESP32-30pin1.d22, R2.Pin_0
  N2: ESP32-30pin1.d15, S1.leg1, R1.Pin_0
  GND: ESP32-30pin1.gnd, ESP32-30pin1.GND, R1.Pin_1, LED1.cathode, R3.Pin_1
  N3: ESP32-30pin1.3V3, S1.leg0, R3.Pin_0
  N4: LED1.anode, R2.Pin_1

custom parts:
  esp32: based on work of Roman Minyaylov, at https://github.com/roman-minyaylov/nodemcu-v3-fritzing
