# Fritzing sketch 7-diode (saved by Fritzing 0.9.3b)
breadboards: 2

parts:
  J1 = Basic Servo
  ESP32-30pin1 = esp32
  R1 = Resistor [tolerance=±5% resistance=2.2k package="0805 [SMD]"]
  VCC1 = Battery block 9V
  U1 = Voltage Regulator - 5V [package="TO220 [THT]"]
  U2 = POT [package=pot_alpha_rv16af-20]
  R2 = Resistor [tolerance=±5% resistance=3k package="2512 [SMD]"]
  C1 = Electrolytic Capacitor [capacitance=0.47mF voltage=50V package="1010 [SMD, electrolytic]"]
  C2 = Electrolytic Capacitor [capacitance=47µF voltage=50V package="1010 [SMD, electrolytic]"]
  C3 = Electrolytic Capacitor [capacitance=4.7µF voltage=50V package="1010 [SMD, electrolytic]"]
  C4 = Electrolytic Capacitor [capacitance=1mF voltage=50V package="1010 [SMD, electrolytic]"]
  C5 = Electrolytic Capacitor [capacitance=1mF voltage=50V package="1010 [SMD, electrolytic]"]
  C6 = Electrolytic Capacitor [capacitance=1mF voltage=50V package="1010 [SMD, electrolytic]"]
  C7 = Electrolytic Capacitor [capacitance=0.47mF voltage=50V package="1010 [SMD, electrolytic]"]
  C8 = Electrolytic Capacitor [capacitance=1mF voltage=50V package="1010 [SMD, electrolytic]"]
  C9 = Electrolytic Capacitor [capacitance=0.47mF voltage=50V package="1010 [SMD, electrolytic]"]
  C10 = Electrolytic Capacitor [capacitance=0.47mF voltage=50V package="1010 [SMD, electrolytic]"]
  C11 = Electrolytic Capacitor [capacitance=1mF voltage=50V package="1010 [SMD, electrolytic]"]
  C12 = Electrolytic Capacitor [capacitance=4.7mF voltage=50V package="1010 [SMD, electrolytic]"]
  D1 = Rectifier Diode [part_number=1N4001 package="300 mil [THT]"]

nets:
  GND: J1.gnd, ESP32-30pin1.gnd, ESP32-30pin1.GND, R1.Pin_1, VCC1.-, U1.GND, U2.E, C1.-, C2.-, C3.-, C4.-, C5.-, C6.-, C7.-, C8.-, C9.-, C10.-, C11.-, C12.-
  N1: J1.vcc, U1.output_voltage, R2.Pin_0, C1.+, D1.anode
  N2: J1.pulse, ESP32-30pin1.d19
  N3: ESP32-30pin1.Vin, C3.+, C4.+, C5.+, C6.+, C7.+, C8.+, C9.+, C10.+, C11.+, C12.+, D1.cathode
  N4: ESP32-30pin1.d32, R1.Pin_0, U2.S
  N5: VCC1.+, U1.input_voltage, C2.+
  N6: U2.A, R2.Pin_1

custom parts:
  esp32: based on work of Roman Minyaylov, at https://github.com/roman-minyaylov/nodemcu-v3-fritzing
