# Fritzing sketch 7.5-caps-right-of-diode (saved by Fritzing 0.9.3b)
circuit board: 8.46667cm x 5.64444cm
breadboards: 2

parts:
  J1 = Basic Servo
  ESP32-30pin1 = esp32
  R1 = Resistor [tolerance=±5% resistance=2.2k package="0805 [SMD]"]
  VCC1 = Battery block 9V
  U1 = Voltage Regulator - 5V [package="TO220 [THT]"]
  U2 = POT [package=pot_alpha_rv16af-20]
  R2 = Resistor [tolerance=±5% resistance=3k package="2512 [SMD]"]
  C1 = Electrolytic Capacitor [capacitance=0.47mF voltage=50V package="1010 [SMD, electrolytic]"]
  C2 = Electrolytic Capacitor [capacitance=47µF voltage=50V package="1010 [SMD, electrolytic]"]
  C4 = Electrolytic Capacitor [capacitance=1mF voltage=50V package="1010 [SMD, electrolytic]"]
  D1 = Rectifier Diode [part_number=1N4001 package="300 mil [THT]"]
  C5 = Electrolytic Capacitor [capacitance=4.7mF package="200 mil [THT, electrolytic]"]

nets:
  GND: J1.gnd, ESP32-30pin1.gnd, ESP32-30pin1.GND, R1.Pin_1, VCC1.-, U1.GND, U2.E, C1.-, C2.-, C4.-, C5.-
  N1: J1.vcc, U1.output_voltage, R2.Pin_0, C1.+, D1.anode
  N2: J1.pulse, ESP32-30pin1.d19
  N3: ESP32-30pin1.Vin, C4.+, D1.cathode, C5.+
  N4: ESP32-30pin1.d32, R1.Pin_0, U2.S
  N5: VCC1.+, U1.input_voltage, C2.+
  N6: U2.A, R2.Pin_1

notes:
  działa, BARDZO rzadko się zrestartuje, ale obniżenie napięcia pwoduje że spada napięcie na potencjometrze a więc zaczyna serwo skakać aż się nie ustabilizuje.

custom parts:
  esp32: based on work of Roman Minyaylov, at https://github.com/roman-minyaylov/nodemcu-v3-fritzing
