# Fritzing sketch 8-rp-attempts (saved by Fritzing 0.9.3b)
circuit board: 8.46667cm x 5.64444cm
breadboards: 2

parts:
  J1 = Basic Servo
  ESP32-30pin1 = esp32
  R1 = Resistor [tolerance=±5% resistance=2.2k package="0805 [SMD]"]
  U1 = Voltage Regulator - 5V [package="TO220 [THT]"]
  U2 = POT [package=pot_alpha_rv16af-20]
  R2 = Resistor [tolerance=±5% resistance=3k package="2512 [SMD]"]
  VCC1 = Battery block 9V
  C1 = Electrolytic Capacitor [capacitance=0.47mF package="100 mil [THT, electrolytic]"]
  C2 = Electrolytic Capacitor [capacitance=0.47mF package="100 mil [THT, electrolytic]"]
  L1 = Inductor [package="400 mil [THT]"]
  C3 = Electrolytic Capacitor [capacitance=0.47mF package="100 mil [THT, electrolytic]"]
  C4 = Electrolytic Capacitor [capacitance=0.47mF package="100 mil [THT, electrolytic]"]
  U3 = Voltage Regulator - 5V [package="TO220 [THT]"]

nets:
  GND: J1.gnd, ESP32-30pin1.gnd, ESP32-30pin1.GND, R1.Pin_1, U1.GND, U2.E, VCC1.-, C1.-, C2.-, C3.-, C4.-, U3.GND
  N1: J1.vcc, U3.output_voltage
  N2: J1.pulse, ESP32-30pin1.d19
  N3: ESP32-30pin1.Vin, U1.output_voltage, R2.Pin_0, C3.+, C4.+
  N4: ESP32-30pin1.d32, R1.Pin_0, U2.S
  N5: U1.input_voltage, C2.+, L1.pin_1
  N6: U2.A, R2.Pin_1
  N7: VCC1.+, C1.+, L1.pin_0, U3.input_voltage

notes:
  niestety - nie spełnia pokładanych nadziei

custom parts:
  esp32: based on work of Roman Minyaylov, at https://github.com/roman-minyaylov/nodemcu-v3-fritzing
