# Fritzing sketch dispenser-holeboard (saved by Fritzing 0.9.6b)
circuit board: 8.46667cm x 5.64444cm
perfboards: 1

parts:
  J1 = Basic Servo
  ESP32-30pin1 = esp32
  R1 = Resistor [tolerance=±5% resistance=470 power=0.25 package=THT]
  U1 = Mini-USB _B_ connector with 5th pin broken out. [package=usb-minib]

nets:
  GND: J1.gnd, ESP32-30pin1.gnd, ESP32-30pin1.GND, R1.Pin_1, U1.MTN2
  N1: J1.vcc, R1.Pin_0, U1.D+
  N2: J1.pulse, ESP32-30pin1.d19

custom parts:
  esp32: based on work of Roman Minyaylov, at https://github.com/roman-minyaylov/nodemcu-v3-fritzing
