# Fritzing sketch button-with-just-resistor (saved by Fritzing 0.9.10b)
circuit board: 8.46667cm x 5.64444cm
perfboards: 1

parts:
  LED1 = LED - 5mm [color="Red (633nm)" current=0.030 package="5 mm [THT]"]
  JP1 = Header 5x2 [package=2x5-ra]
  U1 = LuaNode32 / ESP32 [part_number=ESP32S-PIN30]
  JP2 = Header 2 [package=molex-1x2_lock]
  R2 = Resistor [tolerance=±5% power=0W resistance=200 package=THT]
  R1 = Resistor [tolerance=±5% resistance=6.8k package=THT]
  JP3 = Header 2 [package=molex-1x2_lock]
  S2 = Round Pushbutton
  R5 = Resistor [tolerance=±5% power=0W resistance=330 package=THT]
  R6 = Resistor [tolerance=±5% power=0W resistance=200 package=THT]
  R7 = Resistor [tolerance=±5% power=0W resistance=330 package=THT]

nets:
  GND: LED1.cathode, JP1.1, U1.GND, JP2.2, R1.Pin_1, R6.Pin_1, R7.Pin_1
  N1: LED1.anode, JP2.1, R2.Pin_1, R5.Pin_1
  N2: JP1.9, U1.Vin, R6.Pin_0, R7.Pin_0
  N3: U1.3V3, JP3.2, S2.leg0
  N4: U1.D22, R2.Pin_0, R5.Pin_0
  N5: R1.Pin_0, JP3.1, S2.leg1

custom parts:
  LuaNode32 / ESP32: New Image for LuaNode32 DOIT ESP32 DEVKIT V1. Base parts from LuaNode32 / ESP32 ESP32 based LuaNode32 by G.Noorlander DOIT Esp32 DevKit v1 (30 pins long, 11 pins width) by Werner Rothschopf (modified by vanepp Dec 2018)
