# Fritzing sketch servo-controller-schema (saved by Fritzing 0.9.3b)
circuit board: 8.46667cm x 5.64444cm
breadboards: 2

parts:
  J1 = Basic Servo
  ESP32-30pin1 = esp32
  R1 = Resistor [tolerance=±5% resistance=2.2k package="0805 [SMD]"]
  VCC1 = Battery block 9V
  U2 = POT [part_number=1K package=pot_alpha_rv16af-20]
  R2 = Resistor [tolerance=±5% resistance=3k package="2512 [SMD]"]
  U3 = Voltage Regulator - 3.3V [package="TO220 [THT]"]
  U4 = Voltage Regulator - 5V [package="TO220 [THT]"]
  C2 = Electrolytic Capacitor [capacitance=4.7mF voltage=35V part_number=6000 package="300 mil [THT, electrolytic]"]
  6_8mF = Capacitor Polarized [package=panasonic_g]

nets:
  GND: J1.gnd, ESP32-30pin1.gnd, ESP32-30pin1.GND, R1.Pin_1, VCC1.-, U2.E, U3.GND, U4.GND, C2.-, 6_8mF.-
  N1: J1.vcc, U4.output_voltage, C2.+, 6_8mF.+
  N2: J1.pulse, ESP32-30pin1.d19
  N3: ESP32-30pin1.3V3, R2.Pin_0, U3.output_voltage
  N4: ESP32-30pin1.d32, R1.Pin_0, U2.S
  N5: VCC1.+, U3.input_voltage, U4.input_voltage
  N6: U2.A, R2.Pin_1

notes:
  działa, BARDZO rzadko się zrestartuje, ale obniżenie napięcia pwoduje że spada napięcie na potencjometrze a więc zaczyna serwo skakać aż się nie ustabilizuje.

custom parts:
  esp32: based on work of Roman Minyaylov, at https://github.com/roman-minyaylov/nodemcu-v3-fritzing
